# Fritzing sketch Sketch (saved by Fritzing 0.9.0b)
breadboards: 1

parts:
  Composant1 = Arduino Uno (Rev3)
  Composant2 = Arduino Ethernet Shield (Rev3)
  M1 = DC Motor
  Q1 = npn-Powertransistor [package="TO220 [THT]"]
  VCC1 = Battery block 9V
  D3 = Rectifier Diode [part_number=1N4001 package="300 mil [THT]"]
  R1 = Resistor [tolerance=±5% resistance=220 package=THT]
  R2 = Resistor [tolerance=±5% resistance=470 package=THT]
  LED1 = LED - 5mm [color="Red (633nm)" package="5 mm [THT]"]
  R3 = Rotary Potentiometer (Large) [package=THT]

nets:
  N1: Composant1.A1, R3.wiper
  N2: Composant2.D8, R1.Pin_0, R2.Pin_1
  N3: Composant2.PWM_D9, R3.leg2
  N4: Composant2.GND, Q1.emitter, VCC1.-, LED1.cathode, R3.leg1
  N5: M1.pin_1, VCC1.+, D3.cathode
  N6: M1.pin_2, Q1.collector, D3.anode
  N7: Q1.base, R1.Pin_1
  N8: R2.Pin_0, LED1.anode
